# Fritzing sketch reading-solar-voltage (saved by Fritzing 0.9.3b)
breadboards: 1

parts:
  R2 = Resistor [tolerance=±5% resistance=4.7k package=THT]
  U1 = attiny85 [package=dip]
  D1 = SOLAR-IXYS [package=solarbit-12x1]
  R5 = Resistor [tolerance=±5% resistance=4.7k package=THT]
  MCU1 = Raspberry Pi Zero

nets:
  N1: R2.Pin_0, D1.C
  N2: R2.Pin_1, U1.Pin_7, R5.Pin_0
  N3: U1.Pin_2, MCU1.pin_7, MCU1.pin_8
  N4: U1.Pin_3, U1.Pin_4, D1.A, R5.Pin_1, MCU1.pin_6, MCU1.pin_9, MCU1.pin_10, MCU1.pin_12, MCU1.pin_14, MCU1.pin_30, MCU1.pin_39
  N5: U1.Pin_8, MCU1.pin_1, MCU1.pin_17
